# Fritzing sketch motor-switch (saved by Fritzing 0.9.10b)
breadboards: 1

parts:
  Mod1 = Raspberry Pi 4B  # not connected
  Part1 = Arduino Uno (Rev3)
  Part2 = Arduino Nano (Rev3.0)

nets:
  N1: Part1.A4/SDA, Part2.A4
  N2: Part1.A5/SCL, Part2.A5
